# Fritzing sketch Schema (saved by Fritzing 0.9.2b)
breadboards: 1

parts:
  U1 = ESP8266 WiFi Module [part_number=ESP8266]
  U2 = Breadboard Power Supply [package=THT]
  J1 = Screw terminal - 2 pins [package=THT]
  J2 = Screw terminal - 2 pins [package=THT]
  R1 = Resistor [tolerance=±5% resistance=220 package="2512 [SMD]"]

nets:
  N1: U1.VCC, U1.CH_PD, U2.pin4, J1.pin1
  N2: U1.GPIO_2, J2.pin2, R1.Pin_0
  N3: U1.GND, U2.pin2, R1.Pin_1

notes:
  Water to detect

custom parts:
  ESP8266 WiFi Module: Generic WiFi Module based on the ESP8266 with onboard PCB antenna and UART communications
  Breadboard Power Supply: Représentation Carte Breadboard Power Supply
